# Fritzing sketch CoderDojo_name_shaped_with_Arduino_and_RPi (saved by Fritzing 0.9.1b)

parts:
  Εξάρτημα1 = Arduino Uno (Rev3)  # not connected
  Raspberry_Pi2 = Raspberry Pi B+  # not connected
  Εξάρτημα2 = Arduino Uno (Rev3)  # not connected
  Εξάρτημα3 = Arduino Uno (Rev3)  # not connected
  Raspberry_Pi1 = Raspberry Pi B+  # not connected
  Raspberry_Pi3 = Raspberry Pi B+  # not connected
  Raspberry_Pi4 = Raspberry Pi B+  # not connected
  Εξάρτημα4 = Arduino Uno (Rev3)  # not connected
  Raspberry_Pi5 = Raspberry Pi B+  # not connected
  Raspberry_Pi6 = Raspberry Pi B+  # not connected
  Raspberry_Pi7 = Raspberry Pi B+  # not connected
  Raspberry_Pi8 = Raspberry Pi B+  # not connected
  Εξάρτημα5 = Arduino Uno (Rev3)  # not connected
  Raspberry_Pi9 = Raspberry Pi B+  # not connected
  Raspberry_Pi10 = Raspberry Pi B+  # not connected
  Εξάρτημα6 = Arduino Uno (Rev3)  # not connected
  Raspberry_Pi11 = Raspberry Pi B+  # not connected
  Raspberry_Pi12 = Raspberry Pi B+
  Εξάρτημα7 = Arduino Uno (Rev3)  # not connected
  Εξάρτημα8 = Arduino Uno (Rev3)
  Εξάρτημα9 = Arduino Uno (Rev3)  # not connected
  Εξάρτημα10 = Arduino Uno (Rev3)  # not connected
  Εξάρτημα11 = Arduino Uno (Rev3)  # not connected
  Raspberry_Pi13 = Raspberry Pi B+  # not connected
  Raspberry_Pi14 = Raspberry Pi B+  # not connected
  Εξάρτημα12 = Arduino Uno (Rev3)  # not connected
  Εξάρτημα13 = Arduino Uno (Rev3)  # not connected
  Raspberry_Pi15 = Raspberry Pi B+  # not connected
  Raspberry_Pi16 = Raspberry Pi B+  # not connected
  Εξάρτημα14 = Arduino Uno (Rev3)  # not connected
  Εξάρτημα15 = Arduino Uno (Rev3)  # not connected
  Raspberry_Pi17 = Raspberry Pi B+  # not connected
  Εξάρτημα16 = Arduino Uno (Rev3)  # not connected
  Εξάρτημα17 = Arduino Uno (Rev3)  # not connected
  Εξάρτημα18 = Arduino Uno (Rev3)  # not connected
  Raspberry_Pi18 = Raspberry Pi B+  # not connected
  Raspberry_Pi19 = Raspberry Pi B+  # not connected
  Raspberry_Pi20 = Raspberry Pi B+  # not connected
  Raspberry_Pi21 = Raspberry Pi B+  # not connected
  Εξάρτημα19 = Arduino Uno (Rev3)  # not connected
  Εξάρτημα20 = Arduino Uno (Rev3)  # not connected
  Εξάρτημα21 = Arduino Uno (Rev3)
  Εξάρτημα22 = Arduino Uno (Rev3)  # not connected
  Raspberry_Pi22 = Raspberry Pi B+  # not connected
  Raspberry_Pi23 = Raspberry Pi B+  # not connected
  Raspberry_Pi24 = Raspberry Pi B+
  Raspberry_Pi25 = Raspberry Pi B+  # not connected
  Εξάρτημα23 = Arduino Uno (Rev3)  # not connected
  Εξάρτημα24 = Arduino Uno (Rev3)
  Raspberry_Pi26 = Raspberry Pi B+
  Raspberry_Pi27 = Raspberry Pi B+  # not connected
  Εξάρτημα25 = Arduino Uno (Rev3)  # not connected
  Εξάρτημα26 = Arduino Uno (Rev3)  # not connected
  Εξάρτημα27 = Arduino Uno (Rev3)
  Εξάρτημα28 = Arduino Uno (Rev3)
  Raspberry_Pi28 = Raspberry Pi B+  # not connected
  Raspberry_Pi29 = Raspberry Pi B+
  Raspberry_Pi30 = Raspberry Pi B+  # not connected
  Raspberry_Pi31 = Raspberry Pi B+
  Εξάρτημα29 = Arduino Uno (Rev3)  # not connected

nets:
  N1: Raspberry_Pi12.GPIO9, Εξάρτημα8.A1
  N2: Raspberry_Pi12.GPIO25, Εξάρτημα8.A0
  N3: Εξάρτημα21.A0, Raspberry_Pi24.GPIO25
  N4: Εξάρτημα21.A1, Raspberry_Pi24.GPIO9
  N5: Εξάρτημα24.D3_PWM, Raspberry_Pi26.GPIO13
  N6: Εξάρτημα24.D4, Raspberry_Pi26.GND
  N7: Εξάρτημα27.D3_PWM, Raspberry_Pi29.GPIO13
  N8: Εξάρτημα27.D4, Raspberry_Pi29.GND
  N9: Εξάρτημα28.A0, Raspberry_Pi31.GPIO25
  N10: Εξάρτημα28.A1, Raspberry_Pi31.GPIO9
