# Fritzing sketch football_CoderDojo (saved by Fritzing 0.9.1b)
breadboards: 1

parts:
  Εξάρτημα1 = Arduino Nano (Rev3.0)
  J1 = Basic Servo
  LED1 = RGB LED (com. cathode, rgb) [package="5 mm [THT]"]
  R1 = Resistor [tolerance=±5% resistance=220 package=THT]
  R2 = Resistor [tolerance=±5% resistance=220 package=THT]
  R3 = Resistor [tolerance=±5% resistance=220 package=THT]

nets:
  N1: Εξάρτημα1.D5, R1.Pin_0
  N2: Εξάρτημα1.D6, R2.Pin_0
  N3: Εξάρτημα1.D8, J1.pulse
  N4: Εξάρτημα1.D9, R3.Pin_0
  GND: Εξάρτημα1.GND, J1.gnd, LED1.common_cathode
  5V: Εξάρτημα1.5V, J1.vcc
  N5: LED1.red_anode, R1.Pin_1
  N6: LED1.green_anode, R2.Pin_1
  N7: LED1.blue_anode, R3.Pin_1
