# Fritzing sketch Segment-1Digit-Display_forScratch (saved by Fritzing 0.9.1b)
breadboards: 1

parts:
  7_Segment1 = 7 Segment Display
  7_Segment2 = 7 Segment Display  # not connected
  R1 = Resistor [tolerance=±5% resistance=220 package=THT]
  R2 = Resistor [tolerance=±5% resistance=220 package=THT]
  R3 = Resistor [tolerance=±5% resistance=220 package=THT]
  R4 = Resistor [tolerance=±5% resistance=220 package=THT]
  R5 = Resistor [tolerance=±5% resistance=220 package=THT]
  R8 = Resistor [tolerance=±5% resistance=220 package=THT]
  Εξάρτημα1 = Arduino Uno (Rev3)

nets:
  N1: 7_Segment1.Segment_E, R8.Pin_1
  N2: 7_Segment1.Segment_D, Εξάρτημα1.D13/SCK
  N3: 7_Segment1.common_anode, Εξάρτημα1.GND
  N4: 7_Segment1.Segment_C, R5.Pin_0
  N5: 7_Segment1.Segment_B, R1.Pin_0
  N6: 7_Segment1.Segment_A, R2.Pin_0
  N7: 7_Segment1.Segment_F, R4.Pin_1
  N8: 7_Segment1.Segment_G, R3.Pin_1
  N9: R1.Pin_1, Εξάρτημα1.D12/MISO
  N10: R2.Pin_1, Εξάρτημα1.D11_PWM/MOSI
  N11: R3.Pin_0, Εξάρτημα1.D6_PWM
  N12: R4.Pin_0, Εξάρτημα1.D5_PWM
  N13: R5.Pin_1, Εξάρτημα1.D9_PWM
  N14: R8.Pin_0, Εξάρτημα1.D10_PWM/SS

notes:
  1, 2, 3, 4, 5
  6, 7, 8, 9, 10
  A
  B
  C
  DP
  D
  E
  F
  G
  1 -> E
  2 -> D
  3 -> GND
  4 -> C
  6 -> B
  7 -> A
  8 -> GND
  9 -> F
  10 -> G
  Segment -> Arduino
  7(A) -> 5
  6(B) -> 6
  4(C) -> 9
  2(D) -> 13
  1(E) -> 10
  9(F) -> 11
  10(G) -> 12
  Segment -> Arduino
  μπλε -> 5
  κόκκινο -> 6
  μοβ -> 9
  άσπρο -> 10
  κίτρινο -> 11
  πράσινο -> 12
  πορτοκαλί -> 13
  μαύρο ΠΑΝΤΑ στο GND
  To 5 (DP) το αγνοούμε
  Η Οθόνη αποτελείται από 7 γραμμές LED και μία τελίτσα LED. Για αυτό τόσα πολλά καλώδια για μια μόνο οθονίτσα!
  Έχουμε πει πως ανάμεσα σε κάθε pin στο Arduino και ενός LED βάζουμε μία αντίσταση τουλάχιστον 220Ω. Μόνο στο pin #13 δεν χρειάζεται!
  Πως σχηματίζουμε αριθμούς ανάβοντας τα LED;
  Υπόδειξη: Το "3" είναι με αναμένα τα A+B+C+D+G και σβηστά τα άλλα!

// code stored in the sketch: Segment-1DigitDisplay_easy.ino

