# Fritzing sketch PicachuVsCharmander (saved by Fritzing 0.9.2b)
breadboards: 1

parts:
  Εξάρτημα1 = Arduino Uno (Rev3)
  RGB_Charmander = RGB LED (com. cathode, rgb) [package="5 mm [THT]"]
  RGB_Pikachu = RGB LED (com. cathode, rgb) [package="5 mm [THT]"]
  Button_Jump = Pushbutton [package="[THT]"]
  Button_Attack = Pushbutton [package="[THT]"]
  R1 = Resistor [tolerance=±5% resistance=220 package=THT]
  R2 = Resistor [tolerance=±5% resistance=220 package=THT]
  R3 = Resistor [tolerance=±5% resistance=220 package=THT]
  R4 = Resistor [tolerance=±5% resistance=220 package=THT]
  R5 = Resistor [tolerance=±5% resistance=220 package=THT]
  R6 = Resistor [tolerance=±5% resistance=220 package=THT]
  R7 = Resistor [tolerance=±5% resistance=10k package=THT]
  R8 = Resistor [tolerance=±5% resistance=10k package=THT]

nets:
  N1: Εξάρτημα1.D9_PWM, R1.Pin_0
  N2: Εξάρτημα1.D10_PWM/SS, R6.Pin_0
  N3: Εξάρτημα1.D11_PWM/MOSI, R5.Pin_0
  N4: Εξάρτημα1.D12/MISO, R4.Pin_0
  N5: Εξάρτημα1.GND, RGB_Charmander.common_cathode, RGB_Pikachu.common_cathode, R7.Pin_0, R8.Pin_0
  N6: Εξάρτημα1.D2, Button_Jump.Pin_1, Button_Jump.Pin_2, R8.Pin_1
  N7: Εξάρτημα1.D3_PWM, Button_Attack.Pin_3, Button_Attack.Pin_4, R7.Pin_1
  N8: Εξάρτημα1.D5_PWM, R3.Pin_0
  N9: Εξάρτημα1.D6_PWM, R2.Pin_0
  N10: Εξάρτημα1.5V, Button_Jump.Pin_3, Button_Jump.Pin_4, Button_Attack.Pin_1, Button_Attack.Pin_2
  N11: RGB_Charmander.red_anode, R6.Pin_1
  N12: RGB_Charmander.green_anode, R5.Pin_1
  N13: RGB_Charmander.blue_anode, R4.Pin_1
  N14: RGB_Pikachu.red_anode, R3.Pin_1
  N15: RGB_Pikachu.green_anode, R2.Pin_1
  N16: RGB_Pikachu.blue_anode, R1.Pin_1

notes:
  Pikachu's Life LEDs Pins: A5, A6, A9
  Charmander's Life LEDs Pins: D10, D11, D12
  GREEN = A6, D11
  BLUE = A9, D12
  RED = A5, D10
