# Fritzing sketch PlayMusic (saved by Fritzing 0.9.2b)
breadboards: 1

parts:
  J1 = Piezo Speaker
  Εξάρτημα1 = Arduino Uno (Rev3)

nets:
  N1: J1.pin1, Εξάρτημα1.GND
  N2: J1.pin2, Εξάρτημα1.D3_PWM
