# Fritzing sketch ProtectThePots (saved by Fritzing 0.9.2b)
breadboards: 1

parts:
  Εξάρτημα1 = Arduino Uno (Rev3)
  R1 = Photocell (LDR) [package=THT]
  R2 = Photocell (LDR) [package=THT]
  R3 = Resistor [tolerance=±5% resistance=10k package=THT]
  R4 = Resistor [tolerance=±5% resistance=10k package=THT]

nets:
  N1: Εξάρτημα1.A0, R1.pin_1, R3.Pin_0
  N2: Εξάρτημα1.A1, R2.pin_0, R4.Pin_1
  N3: Εξάρτημα1.5V, R1.pin_0, R2.pin_1
  N4: Εξάρτημα1.GND, R3.Pin_1, R4.Pin_0

notes:
  2 Φωτοαντιστάσεις
  2 Αντιστάσεις τουλάχιστον 10KΩ
