# Fritzing sketch GameBoard_Sketch (saved by Fritzing 0.9.1b)
breadboards: 1

parts:
  Εξάρτημα1 = Arduino Uno (Rev3)
  LED1 = LED - 5mm [color="Red (633nm)" package="5 mm [THT]"]
  LED2 = LED - 5mm [color="Green (555nm)" package="5 mm [THT]"]
  R1 = Resistor [tolerance=±5% resistance=220 package=THT]
  R2 = Resistor [tolerance=±5% resistance=220 package=THT]
  J1 = Basic Servo

nets:
  N1: Εξάρτημα1.D10_PWM/SS, R1.Pin_0
  N2: Εξάρτημα1.D11_PWM/MOSI, R2.Pin_0
  GND: Εξάρτημα1.GND, LED1.cathode, LED2.cathode, J1.gnd
  N3: Εξάρτημα1.D4, J1.pulse
  5V: Εξάρτημα1.5V, J1.vcc
  N4: LED1.anode, R2.Pin_1
  N5: LED2.anode, R1.Pin_1
