# Fritzing sketch Shadow LED (saved by Fritzing 0.9.2b)
breadboards: 1

parts:
  R1 = Photocell (LDR) [package=THT]
  R2 = Resistor [tolerance=±5% resistance=10k package=THT]
  LED1 = RGB LED (com. cathode, rgb) [package="5 mm [THT]"]
  R3 = Resistor [tolerance=±5% resistance=220 package=THT]
  R4 = Resistor [tolerance=±5% resistance=220 package=THT]
  R5 = Resistor [tolerance=±5% resistance=220 package=THT]
  Εξάρτημα1 = Arduino Uno (Rev3)

nets:
  N1: R1.pin_0, R2.Pin_1, Εξάρτημα1.A1
  N2: R1.pin_1, Εξάρτημα1.5V
  N3: R2.Pin_0, LED1.common_cathode, Εξάρτημα1.GND
  N4: LED1.red_anode, R3.Pin_1
  N5: LED1.green_anode, R4.Pin_1
  N6: LED1.blue_anode, R5.Pin_1
  N7: R3.Pin_0, Εξάρτημα1.D6_PWM
  N8: R4.Pin_0, Εξάρτημα1.D4
  N9: R5.Pin_0, Εξάρτημα1.D3_PWM

notes:
  1 RGB LED
  1 φωτοαντίσταση
  3 αντιστάσεις 220Ω
  1 αντίσταση 10ΚΩ
