# Fritzing sketch Cubes Addition NFC (saved by Fritzing 0.9.1b)
breadboards: 1

parts:
  7_Segment1 = 7 Segment Display
  7_Segment2 = 7 Segment Display  # not connected
  R1 = Resistor [tolerance=±5% resistance=220 package=THT]
  R2 = Resistor [tolerance=±5% resistance=220 package=THT]
  R3 = Resistor [tolerance=±5% resistance=220 package=THT]
  R4 = Resistor [tolerance=±5% resistance=220 package=THT]
  R5 = Resistor [tolerance=±5% resistance=220 package=THT]
  R6 = Resistor [tolerance=±5% resistance=220 package=THT]
  R7 = Resistor [tolerance=±5% resistance=220 package=THT]
  R8 = Resistor [tolerance=±5% resistance=220 package=THT]
  Εξάρτημα1 = Arduino Uno (Rev3)

nets:
  N1: 7_Segment1.Segment_E, R8.Pin_1
  N2: 7_Segment1.Segment_D, R7.Pin_1
  N3: 7_Segment1.common_anode, Εξάρτημα1.GND
  N4: 7_Segment1.Segment_C, R5.Pin_0
  N5: 7_Segment1.Segment_DP, R6.Pin_0
  N6: 7_Segment1.Segment_B, R1.Pin_0
  N7: 7_Segment1.Segment_A, R2.Pin_0
  N8: 7_Segment1.Segment_F, R4.Pin_1
  N9: 7_Segment1.Segment_G, R3.Pin_1
  N10: R1.Pin_1, Εξάρτημα1.D8
  N11: R2.Pin_1, Εξάρτημα1.D7
  N12: R3.Pin_0, Εξάρτημα1.D3_PWM
  N13: R4.Pin_0, Εξάρτημα1.D2
  N14: R5.Pin_1, Εξάρτημα1.D4
  N15: R6.Pin_1, Εξάρτημα1.D9_PWM
  N16: R7.Pin_0, Εξάρτημα1.D5_PWM
  N17: R8.Pin_0, Εξάρτημα1.D6_PWM

notes:
  1, 2, 3, 4, 5
  6, 7, 8, 9, 10
  A
  B
  C
  DP
  D
  E
  F
  G
  1 -> E
  2 -> D
  3 -> GND
  4 -> C
  5 -> DP
  6 -> B
  7 -> A
  8 -> GND
  9 -> F
  10 -> G
  Segment -> Arduino
  7(A) -> 5
  6(B) -> 6
  4(C) -> 7
  2(D) -> 8
  1(E) -> 9
  9(F) -> 10
  10(G) -> 11
  5(DP) -> 12
  Segment -> Arduino
  μπλε -> 5
  κόκκινο -> 6
  μοβ -> 7
  γκρι -> 8
  άσπρο -> 9
  κίτρινο -> 10
  πράσινο -> 11
  πορτοκαλί -> 12
  μαύρο ΠΑΝΤΑ στο GND
  Vin
  GND
  SCK
  MISO
  MOSI
  NSS
  PN532 > (χρώμα) > Arduino
  NSS > καφέ > 10
  MOSI > γκρι > 11
  MISO > μοβ > 12
  SCK > κυανό > 13
  Vin > κόκκινο > 5V
  GND > μαύρο > GND
  PN532 NFC Module
  from epalsite.com
  compatible with 5V and 3.3v

// code stored in the sketch: Segment-1DigitDisplay_easy.ino
// Easy to understand example for Arduino 7 segment display

void setup() {              
	pinMode(2, OUTPUT); 
	pinMode(3, OUTPUT);
	pinMode(4, OUTPUT);
	pinMode(5, OUTPUT);
	pinMode(6, OUTPUT);
	pinMode(7, OUTPUT);
	pinMode(8, OUTPUT);
	pinMode(9, OUTPUT);
	digitalWrite(9, 0);  // start with the "dot" off
}

void loop() {
	// write '9'
	digitalWrite(2, 1);
	digitalWrite(3, 1);
	digitalWrite(4, 1);
	digitalWrite(5, 0);
	digitalWrite(6, 0);
	digitalWrite(7, 1);
	digitalWrite(8, 1);
	delay(1000);

	// write '8'
	digitalWrite(2, 1);
	digitalWrite(3, 1);
	digitalWrite(4, 1);
	digitalWrite(5, 1);
	digitalWrite(6, 1);
	digitalWrite(7, 1);
	digitalWrite(8, 1);
	delay(1000);

	// write '7'
	digitalWrite(2, 1);
	digitalWrite(3, 1);
	digitalWrite(4, 1);
	digitalWrite(5, 0);
	digitalWrite(6, 0);
	digitalWrite(7, 0);
	digitalWrite(8, 0);
	delay(1000);

	// write '6'
	digitalWrite(2, 1);
	digitalWrite(3, 0);
	digitalWrite(4, 1);
	digitalWrite(5, 1);
	digitalWrite(6, 1);
	digitalWrite(7, 1);
	digitalWrite(8, 1);
	delay(1000);

	// write '5'
	digitalWrite(2, 1);
	digitalWrite(3, 0);
	digitalWrite(4, 1);
	digitalWrite(5, 1);
	digitalWrite(6, 0);
	digitalWrite(7, 1);
	digitalWrite(8, 1);
	delay(1000);

	// write '4'
	digitalWrite(2, 0);
	digitalWrite(3, 1);
	digitalWrite(4, 1);
	digitalWrite(5, 0);
	digitalWrite(6, 0);
	digitalWrite(7, 1);
	digitalWrite(8, 1);
	delay(1000);

	// write '3'
	digitalWrite(2, 1);
	digitalWrite(3, 1);
	digitalWrite(4, 1);
	digitalWrite(5, 1);
	digitalWrite(6, 0);
	digitalWrite(7, 0);
	digitalWrite(8, 1);
	delay(1000);

	// write '2'
	digitalWrite(2, 1);
	digitalWrite(3, 1);
	digitalWrite(4, 0);
	digitalWrite(5, 1);
	digitalWrite(6, 1);
	digitalWrite(7, 0);
	digitalWrite(8, 1);
	delay(1000);

	// write '1'
	digitalWrite(2, 0);
	digitalWrite(3, 1);
	digitalWrite(4, 1);
	digitalWrite(5, 0);
	digitalWrite(6, 0);
	digitalWrite(7, 0);
	digitalWrite(8, 0);
	delay(1000);
	
	// write '0'
	digitalWrite(2, 1);
	digitalWrite(3, 1);
	digitalWrite(4, 1);
	digitalWrite(5, 1);
	digitalWrite(6, 1);
	digitalWrite(7, 1);
	digitalWrite(8, 0);
	delay(4000);
}
